# Fritzing sketch Project 2 (saved by Fritzing 0.9.8b)
breadboards: 1

parts:
  Mod1 = Raspberry Pi 4B
  LED1 = LED - 5mm [color="Red (633nm)" current=0.030 package="5 mm [THT]"]
  R1 = Resistor [tolerance=±5% power=0.25 resistance=220 package=THT]
  S1 = Pushbutton [package="[THT]"]

nets:
  N1: Mod1.GND, R1.Pin_0, S1.Pin_1, S1.Pin_2
  N2: Mod1.GPIO17, LED1.anode
  N3: Mod1.GPIO27, S1.Pin_3, S1.Pin_4
  N4: LED1.cathode, R1.Pin_1
